# Fritzing sketch IoT_Project_Hamza (saved by Fritzing 0.9.3b)
breadboards: 1

parts:
  WeMos_D1_R1 = WeMos D1 R2
  DHT1_(Room) = DHT11 Humitidy and Temperature Sensor
  RFID-RC522 = RFID-RC522-v2
  R1 = Resistor [tolerance=±5% resistance=220 package="1206 [SMD]"]
  DHT2_(Outside) = DHT11 Humitidy and Temperature Sensor
  LED = LED - 3mm [color="Red (633nm)" package="3 mm [THT]"]

nets:
  N1: WeMos_D1_R1.D2, DHT2_(Outside).DATA
  N2: WeMos_D1_R1.D3, DHT1_(Room).DATA
  N3: WeMos_D1_R1.D4, R1.Pin_1
  N4: WeMos_D1_R1.D9, RFID-RC522.RST
  N5: WeMos_D1_R1.D10, RFID-RC522.SDA
  N6: WeMos_D1_R1.D11, RFID-RC522.MOSI
  N7: WeMos_D1_R1.D12, RFID-RC522.MISO
  N8: WeMos_D1_R1.D13, RFID-RC522.SCK
  GND: WeMos_D1_R1.GND, DHT1_(Room).GND, RFID-RC522.GND, DHT2_(Outside).GND, LED.cathode
  VDD: WeMos_D1_R1.5V, DHT1_(Room).VDD, DHT2_(Outside).VDD
  3.3V: WeMos_D1_R1.3.3V, RFID-RC522.3.3V
  N9: R1.Pin_0, LED.anode

custom parts:
  WeMos D1 R2: The D1 R2 is a mini wifi board based on the ESP-8266EX.
  DHT11 Humitidy and Temperature Sensor: DHT11 Humidity and Temperature Sensor
  RFID-RC522-v2: A simple China made RFID-RC522 Reader; do check the pin labels, as this is a MFRC522 based clone.

// code stored in the sketch: Code.ino
#include <ESP8266WiFi.h> // library needed for WiFi setup
#include <PubSubClient.h> // library needed for publish/subsribe to MQTT server as a client
#include "DHT.h" // libary needed for DHT11 temperature sensores
#include<SPI.h> // libary needed for RFID function
#include<MFRC522.h> // libary needed for RFID sensor

#define DHTTYPE DHT11   // DHT sensor type : DHT 11


//RFID



//creating mfrc522 instance
#define RSTPIN 2
#define SSPIN 15
MFRC522 rc(SSPIN, RSTPIN);

int readsuccess;

/* the following are the UIDs of the card which are authorised
    to know the UID of your card/tag use the example code 'DumpInfo'
    from the library mfrc522 it give the UID of the card as well as 
    other information in the card on the serial monitor of the arduino*/

byte defcard[][4]={{0xD0,0x9A,0xC4,0xA3},{0x2A,0xE8,0x7D,0x63}}; //for multiple cards, new ID cards should be added here to be authorized
int N=2; //change this to the number of cards/tags you will use (number of above IDs)
byte readcard[4]; //stores the UID of current tag which is read

//function to get the UID of the card
int getid(){  
  if(!rc.PICC_IsNewCardPresent()){
    return 0;
  }
  if(!rc.PICC_ReadCardSerial()){
    return 0;
  }
 
  
  Serial.println("THE UID OF THE SCANNED CARD IS:");
  
  for(int i=0;i<4;i++){
    readcard[i]=rc.uid.uidByte[i]; //storing the UID of the tag in readcard
    Serial.print(readcard[i],HEX);
  }
   Serial.println("");
   Serial.println("Now Comparing with Authorised cards");
  rc.PICC_HaltA();
  
  return 1;
}

int uidnum=99;
//*****************************************************************************




// Change the credentials below, so your ESP8266 connects to your router
const char* ssid = "AndroidAP";
const char* password = "hamooz1234";

// Change the variable to your VM Ubunitu IP address, so it connects to your MQTT broker
const char* mqtt_server = "192.168.43.211";

// Initializes the espClient. You should change the espClient name if you have multiple ESPs running in your home automation system
WiFiClient espClient;
PubSubClient client(espClient);

// DHT Sensor - GPIO 5 = D1 on ESP-12E NodeMCU board
const int DHTPin = 5;
const int DHTPin2 = 16;

// Lamp - LED - GPIO 4 = D2 on ESP-12E NodeMCU board
const int lamp = 4;
int ledblink=0; //for blinking loop
int mod=5; //for AC mode heating / cooling / off
float difference; // tempreture diffrence
int am=1; // AC auto=1/manual=0 mode

// Initialize DHT sensor.
DHT dht(DHTPin, DHTTYPE);
DHT dht2(DHTPin2, DHTTYPE);

// Timers auxiliar variables
long now = millis();
long lastMeasure = 0;

// Don't change the function below. This functions connects your ESP8266 to your router
void setup_wifi() {
  delay(10);
  // We start by connecting to a WiFi network
  Serial.println();
  Serial.print("Connecting to ");
  Serial.println(ssid);
  WiFi.begin(ssid, password);
  while (WiFi.status() != WL_CONNECTED) {
    delay(500);
    Serial.print(".");
  }
  Serial.println("");
  Serial.print("WiFi connected - ESP IP address: ");
  Serial.println(WiFi.localIP());
}

// This functions is executed when some device publishes a message to a topic that your ESP8266 is subscribed to
// Change the function below to add logic to your program, so when a device publishes a message to a topic that 
// your ESP8266 is subscribed you can actually do something
void callback(String topic, byte* message, unsigned int length) {
  Serial.print("Message arrived on topic: ");
  Serial.print(topic);
  Serial.print(". Message: ");
  String messageTemp;
  
  for (int i = 0; i < length; i++) {
    Serial.print((char)message[i]);
    messageTemp += (char)message[i];
  }
  Serial.println();

  // Feel free to add more if statements to control more GPIOs with MQTT

  // If a message is received on the topic room/lamp2, you check if the message is either on or off. Turns the lamp GPIO according to the message
  if(topic=="room/lamp2"){
      Serial.print("Changing mode to ");
      if(messageTemp == "on"){
        am=1;
        Serial.print("auto");
      }
      else if(messageTemp == "off"){
        am=0;
        mod=3;
        Serial.print("manual");
      }
  }
  //If auto mode is off
  if(am==0){
    // If a message is received on the topic "room/lamp", you check if the message is either on or off. Turns the lamp GPIO according to the message
  if(topic=="room/lamp"){
      Serial.print("Changing Room lamp to ");
      if(messageTemp == "on"){
        digitalWrite(lamp, HIGH);
        Serial.print("On");
      }
      else if(messageTemp == "off"){
        digitalWrite(lamp, LOW);
        Serial.print("Off");
      }
  }
  }
  Serial.println();
}

// This functions reconnects your ESP8266 to your MQTT broker
// Change the function below if you want to subscribe to more topics with your ESP8266 
void reconnect() {
  // Loop until we're reconnected
  while (!client.connected()) {
    Serial.print("Attempting MQTT connection...");
    // Attempt to connect
    if (client.connect("ESP8266Client")) {
      Serial.println("connected");  
      // Subscribe or resubscribe to a topic
      // You can subscribe to more topics (to control more LEDs in this example) ****************************
      client.subscribe("room/lamp"); // Subscribing to Topic "room/lamp" used to switch the A/C (LED) ON/OFF by the IoT dashboard "A/C Remote Switch"
      client.subscribe("room/lamp2"); // Subscribing to Topic "room/lamp2" used to control the A/C mode (OFF: Manual Switch || ON: Auto Balancing Mode) by IoT dashboard "A/C Auto Balancing Mode" Switch 
    } else {
      Serial.print("failed, rc=");
      Serial.print(client.state());
      Serial.println(" try again in 5 seconds");
      // Wait 5 seconds before retrying
      delay(5000);
    }
  }
}

// The setup function sets your ESP GPIOs to Outputs, starts the serial communication at a baud rate of 115200
// Sets your mqtt broker and sets the callback function
// The callback function is what receives messages and actually controls the LEDs
void setup() {
  pinMode(lamp, OUTPUT);
  
  dht.begin();
  
  Serial.begin(115200); //set baud rate for serial communication between arduino and c to 115200
  setup_wifi(); // call the function to connect the wifi
  client.setServer(mqtt_server, 1883); //connect to mqtt server using ip and port
  client.setCallback(callback); //run the procedure for resiving topics from mqtt server


  SPI.begin();
  rc.PCD_Init(); //initialize the receiver  
  rc.PCD_DumpVersionToSerial(); //show details of card reader module

}

// For this project, you don't need to change anything in the loop function. Basically it ensures that you ESP is connected to your broker
void loop() {


//keep cheking if wifi and mqtt is still connected
  if (!client.connected()) {
    reconnect();
  }
  if(!client.loop())
    client.connect("ESP8266Client");

  now = millis();
  // Publishes new temperature and humidity every 10 seconds
  if (now - lastMeasure > 10000) {
    lastMeasure = now;
    // Sensor readings may also be up to 2 seconds 'old' (its a very slow sensor)
    float h = dht.readHumidity();
    float h2 = dht2.readHumidity();

    // Read temperature as Celsius (the default)
    float t = dht.readTemperature();
    float t2 = dht2.readTemperature();
    // Read temperature as Fahrenheit (isFahrenheit = true)
    float f = dht.readTemperature(true);
    float f2 = dht2.readTemperature(true);

    // Check if any reads failed and exit early (to try again).
    if (isnan(h) || isnan(t) || isnan(f)) {
      Serial.println("Failed to read from DHT sensor!");
      return;
    }

    if (isnan(h2) || isnan(t2) || isnan(f2)) {
      Serial.println("Failed to read from DHT2 sensor!");
      return;
    }
    

    // Computes temperature values in Celsius
    float hic = dht.computeHeatIndex(t, h, false);
    float hic2 = dht2.computeHeatIndex(t2, h2, false);

    static char temperatureTemp[7];
    static char temperatureTemp2[7];

    dtostrf(hic, 6, 2, temperatureTemp);
    dtostrf(hic2, 6, 2, temperatureTemp2);

    static char humidityTemp[7];
    static char humidityTemp2[7];
    dtostrf(h, 6, 2, humidityTemp);
    dtostrf(h2, 6, 2, humidityTemp2);

    // Publishes Temperature and Humidity values
    client.publish("room/temperature", temperatureTemp);
    client.publish("room/temperature2", temperatureTemp2);

    client.publish("room/humidity", humidityTemp);
    client.publish("room/humidity2", humidityTemp2);

    Serial.print("Humidity: ");
    Serial.print(h);
    Serial.print(" %\t Temperature: ");
    Serial.print(t);
    Serial.print(" *C ");
    Serial.print(f);
    Serial.print(" *F\t Heat index: ");
    Serial.print(hic);
    Serial.println(" *C ");

    Serial.print("Humidity2: ");
    Serial.print(h2);
    Serial.print(" %\t Temperature2: ");
    Serial.print(t2);
    Serial.print(" *C ");
    Serial.print(f2);
    Serial.print(" *F\t Heat index: ");
    Serial.print(hic2);
    Serial.println(" *C ");
    // Serial.print(hif);
    // Serial.println(" *F");

    if ((t > t2 || t2 > t)&& am == 1){ // Comparing the difference in temperature and powering A/C when difference is more than 2 degrees (IF A/C MODE IS AUTO "am=1"), also publish the LED again
    difference = t - t2;
    if (difference > 2) { // if Room Temp is more than 2 degree higher than Outside Temp --> A/C will start COOLING to achieve balanced temp
      Serial.println("A/C Cooling ON...");
      digitalWrite(lamp, HIGH); // 
      mod=0; //mode for cooling
      client.publish("room/lamp3", "on"); // update A/C Switch as ON
      client.publish("room/lamp4", "Cooling is Active");

      } else if (difference < -2) { // if Room Temp is 2 degrees lower than Outside Temp --> A/C will start Heating the room to achieve balanced temp
        Serial.println("A/C Heating ON...");
        //digitalWrite(lamp, HIGH); //
        mod=1; //mode for heating
        client.publish("room/lamp3", "on"); // update A/C Switch as ON
        client.publish("room/lamp4", "Heating is Active");

        } else {
          Serial.println("Balanced Temperature... A/C OFF");
          digitalWrite(lamp, LOW);
          mod=2;//mode for off
          client.publish("room/lamp3", "off"); //turn off light
        }

   
     }
  }

    if(mod==1){ //if mode is heating blink led to show it is heating not cooling
        if (ledblink == 1) {
          digitalWrite(lamp, LOW);
          ledblink=0;
          // turn LED OFF
        } else {
           digitalWrite(lamp, HIGH);  // turn LED ON
           ledblink=1;
        }
    }
        delay (300);

  readsuccess = getid();

  if(readsuccess){
 
  int match=0;
//this is the part where compare the current tag with pre defined tags
  for(int i=0;i<N;i++){
    Serial.print("Testing Against Authorised card no: ");
    Serial.println(i+1);
    if(!memcmp(readcard,defcard[i],4)){
      match++;
      uidnum=i; // shows the sequence number of the readed card based on defined IDs list after comparing it with this list at beggining. 
      }
    
  }
    
   if(match){
    Serial.println("CARD AUTHORISED"); // if readed card matchs one of the defined cards, then it is an authorized card/tag
    switch(uidnum){ 
      case(0):Serial.println("D09AC4A3");client.publish("room/rfid","Hamza Card D09AC4A3");break; // in case uidnum=0, then will print and publich the UID at index 0 (1st UID) on the pre-defined list "defcard"
      case(1):Serial.println("2AE87D63");client.publish("room/rfid","Hamza Tag 2AE87D63");break;  // in case uidnum=1, then will print and publich the UID at index 1 (2nd UID) on the pre-defined list "defcard"
      // more cases "for example: case(2)" should be added here as well if new UIDs are added in the UID pre-defined list "defcard" 
    }

        }
     else {
      Serial.println("CARD NOT Authorised"); // if readed card DO NOT match any of the defined cards, then print NOT authorized card
      client.publish("room/rfid","Not authorized"); // publish card not authorized
      }
  
  }

   
}
